# Fritzing sketch schema (saved by Fritzing 0.9.4)

parts:
  Part4 = Adafruit Music Maker FeatherWing with Amp [part_number="Adafruit #3436"]
  SP1 = SPEAKER [package=pcb_mount_speaker]
  Part5 = Arduino Nano 33 BLE Sense

nets:
  N1: Part4.OUT_RIGHT+, SP1.+
  N2: Part4.OUT_RIGHT-, SP1.-
  N3: Part4.SD_CS, Part5.D5~
  N4: Part4.MOSI, Part5.D12~/MISO
  GND: Part4.GND, Part5.GND
  3.3V: Part4.3.3V, Part5.3V3
  N5: Part4.MISO, Part5.D11/MOSI, Part5.+5V
  N6: Part4.MP3CS, Part5.D6~
  N7: Part4.DREQ, Part5.D9~
  N8: Part4.XDCS, Part5.D10~

custom parts:
  Adafruit Music Maker FeatherWing with Amp: Bend all audio files to your will with the Adafruit Music Maker FeatherWing + Amplifier! It's a fun-size version of our Music Maker shield for Arduino, and similar to our other Music Maker FeatherWing, but this one is even better - with an on-board 3 Watt amplifier! This powerful wing features the VS1053, an encoding/decoding (codec) chip that can decode a wide variety of audio formats such as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
  Arduino Nano 33 BLE Sense: The Nano 33 BLE Sense (without headers) is Arduino’s 3.3V AI enabled board in the smallest available form factor: 45x18mm! The Arduino Nano 33 BLE Sense is a completely new board on a well-known form factor. It comes with a series of embedded sensors: 9 axis inertial sensor: what makes this board ideal for wearable devices humidity, and temperature sensor: to get highly accurate measurements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
